// Logisim project TestingShifter.circ as structural Verilog: 1 circuit, main circuit main
module main (
  input  in_1,
  output out_2,
  output out_3,
  output out_4,
  output out_5,
  output out_6,
  output [4:0] out_7
);

  wire button_1_out, clock_1_out, xor_1_out, xor_2_out, xor_3_out, xor_4_out, xor_5_out;

  Clock clock_1 (.out(clock_1_out));
  xor xor_1 (xor_1_out, xor_2_out, out_6);
  D_Flip_Flop d_ff_1 (.clk(clock_1_out), .D(xor_1_out), .Q(out_6), .preset(in_1));  // open: Qn, en, reset
  xor xor_2 (xor_2_out, xor_3_out, out_5);
  D_Flip_Flop d_ff_2 (.clk(clock_1_out), .D(out_6), .Q(out_5), .reset(in_1));  // open: Qn, preset, en
  xor xor_3 (xor_3_out, xor_4_out, out_4);
  D_Flip_Flop d_ff_3 (.clk(clock_1_out), .D(out_5), .Q(out_4), .preset(in_1));  // open: Qn, en, reset
  xor xor_4 (xor_4_out, xor_5_out, out_3);
  D_Flip_Flop d_ff_4 (.clk(clock_1_out), .D(out_4), .Q(out_3), .preset(in_1));  // open: Qn, en, reset
  xor xor_5 (xor_5_out, button_1_out, out_2);
  D_Flip_Flop d_ff_5 (.clk(clock_1_out), .D(out_3), .Q(out_2), .reset(in_1));  // open: Qn, preset, en
  Button button_1 (.out(button_1_out));

  assign out_7 = {out_6, out_5, out_4, out_3, out_2};
endmodule
